# Fritzing sketch circuit_diagram (saved by Fritzing 0.9.4)
breadboards: 1

parts:
  U1 = lolin
  DHT1 = DHT22 Humidity and Temperature Sensor
  SparkFun_Air_Quality_Breakout_-_CCS1 = SparkFun Air Quality Breakout - CCS811 [part_number="SEN-14193 "]

nets:
  N1: U1.connector22, DHT1.DATA
  N2: U1.connector32, SparkFun_Air_Quality_Breakout_-_CCS1.SDA
  N3: U1.connector33, SparkFun_Air_Quality_Breakout_-_CCS1.SCL
  VDD: U1.connector34, DHT1.VDD, SparkFun_Air_Quality_Breakout_-_CCS1.3.3V
  GND: U1.connector37, DHT1.GND, SparkFun_Air_Quality_Breakout_-_CCS1.GND

custom parts:
  SparkFun Air Quality Breakout - CCS811: The CCS811 Air Quality Breakout is a digital gas sensor solution that senses a wide range of Total Volatile Organic Compounds (TVOCs), including equivalent carbon dioxide (eCO2) and metal oxide (MOX) levels. VOCs are often categorized as pollutants and/or sensory irritants and can come from a variety of sources like construction materials (paint, carpet, etc.), machines (copiers, processors,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
